# Fritzing sketch LegoEsp32SunTracker (saved by Fritzing 0.9.10b)
breadboards: 1

parts:
  U1 = ESP32S-HiLetgo [part_number=ESP32S-HiLetgo]
  R17 = PHOTOCELL [package=photocell-kit]
  R18 = PHOTOCELL [package=photocell-kit]
  R19 = PHOTOCELL [package=photocell-kit]
  R20 = PHOTOCELL [package=photocell-kit]
  R21 = Resistor [tolerance=±5% resistance=10k power=0.25 package=THT]
  R22 = Resistor [tolerance=±5% resistance=10k power=0.25 package=THT]
  R23 = Resistor [tolerance=±5% resistance=10k power=0.25 package=THT]
  R24 = Resistor [tolerance=±5% resistance=10k power=0.25 package=THT]
  Altitude = Dagu DGServo 9g (Top view) [part_number=RS001B]
  Azimuth = Dagu DGServo 9g (Top view) [part_number=RS001B]

nets:
  N1: U1.EN, R20.P$1, R23.Pin_1
  N2: U1.GPIO36, R19.P$1, R22.Pin_1
  N3: U1.GPIO39, R18.P$2, R21.Pin_0
  N4: U1.GPIO34, R17.P$2, R24.Pin_0
  N5: U1.GND, Altitude.pulse
  N6: U1.GPIO11, R21.Pin_1, R22.Pin_0, R23.Pin_0, R24.Pin_1
  VCC: U1.GPIO6, R17.P$1, R18.P$1, R19.P$2, R20.P$2, Altitude.vcc, Azimuth.vcc
  GND: U1.GPIO7, Altitude.gnd, Azimuth.gnd
  N7: U1.GPIO23, Azimuth.pulse

custom parts:
  ESP32S-HiLetgo: HiLetgo ESP-WROOM-32 ESP32 ESP-32S Development Board 2.4GHz Dual-Mode WiFi + Bluetooth Dual Cores Microcontroller The ESP32 integrated with Antenna switches, RF Balun, power amplifiers, low-noise amplifiers, filters, and management modules, and the entire solution occupies the least area of PCB. 2.4 GHz Wi-Fi plus Bluetooth dual-mode chip, with TSMC Ultra-low power consumption 40nm technology,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
